# Fritzing sketch stabilizer_nano (saved by Fritzing 0.9.4)
breadboards: 1
perfboards: 1

parts:
  Part3 = InvenSense MPU6050
  Part2 = Arduino Nano (Rev3.0)
  J2 = Basic Servo
  J3 = Basic Servo
  U1 = LIPO-2000mAh [package=lipo-2000]
  Part5 = Arduino Nano (Rev3.0)
  Part6 = InvenSense MPU6050
  J4 = Dagu DGServo 9g header (male) [package=THT]
  J5 = Dagu DGServo 9g header (male) [package=THT]
  J6 = Dagu DGServo 9g header (male) [package=THT]
  J7 = Dagu DGServo 9g header (male) [package=THT]
  J8 = Dagu DGServo 9g header (male) [package=THT]

nets:
  VCC: Part3.VCC, Part2.VIN, J2.vcc, J3.vcc, U1.+
  GND: Part3.GND, Part2.GND, J2.gnd, J3.gnd, U1.-
  N1: Part3.SCL, Part2.A5
  N2: Part3.SDA, Part2.A4
  N3: Part3.INT, Part2.D2
  N4: Part2.D5, J3.pulse
  N5: Part2.D6, J2.pulse
  N6: Part5.D2, J4.gnd
  N7: Part5.D8, J5.pulse
  N8: Part5.D9, J6.pulse
  N9: Part5.D10, J7.pulse
  N10: Part5.D11/MOSI, J8.pulse
  N11: Part5.A5, Part6.SCL
  N12: Part5.A4, Part6.SDA
