# Fritzing sketch stabilizer_nano (saved by Fritzing 0.9.4)
breadboards: 1

parts:
  Part3 = InvenSense MPU6050
  Part2 = Arduino Nano (Rev3.0)
  Mod1 = flyskyr6b_1
  J2 = Basic Servo
  J3 = Basic Servo

nets:
  VCC: Part3.VCC, Part2.5V
  GND: Part3.GND, Part2.GND
  N1: Part3.SCL, Part2.A5
  N2: Part3.SDA, Part2.A4
  N3: Part3.INT, Part2.D2
  N4: Part2.D5, J3.pulse
  N5: Part2.D6, J2.pulse
  N6: Part2.D8, Mod1.connector0
  N7: Part2.D9, Mod1.connector1
  N8: Part2.D10, Mod1.connector2
  N9: Part2.D11/MOSI, Mod1.connector4
  N10: Mod1.connector14, Mod1.connector15, Mod1.connector16, Mod1.connector18, J3.gnd
